// Logisim project contadordesc.circ as structural Verilog: 1 circuit, main circuit main
module main (
  input  clk,
  output Q0,
  output Q1,
  output Q2
);

  J_K_Flip_Flop j_k_ff_1 (.J(1'b1), .clk(clk), .K(1'b1), .Qn(Q0));  // open: Q, preset, en, reset
  J_K_Flip_Flop j_k_ff_2 (.J(Q0), .clk(clk), .K(Q0), .Qn(Q1));  // open: Q, preset, en, reset
  J_K_Flip_Flop j_k_ff_3 (.J(Q1), .clk(clk), .K(Q1), .Qn(Q2));  // open: Q, preset, en, reset
  J_K_Flip_Flop j_k_ff_4 (.J(Q2), .clk(clk), .K(Q2));  // open: Q, Qn, preset, en, reset
endmodule
