// Logisim project parity.circ as structural Verilog: 1 circuit, main circuit main
module main (
  input  D0,
  input  D1,
  input  D2,
  input  D3,
  input  SHIFT_LOAD,
  input  CLK,
  output Q3,
  output Q0,
  output Q1,
  output Q2
);

  wire FF0_q, FF1_q, FF2_q, g2_out, g3_out, g4_out, g5_out, g6_out, g7_out, not_1_out;

  D_Flip_Flop FF0 (.clk(CLK), .D(Q0), .Q(FF0_q));  // open: Qn, preset, en, reset
  not not_1 (not_1_out, SHIFT_LOAD);
  and g1 (Q0, D0, not_1_out);
  and g5 (g5_out, FF0_q, SHIFT_LOAD);
  and g2 (g2_out, not_1_out, D1);
  or or_1 (Q1, g5_out, g2_out);
  D_Flip_Flop FF1 (.clk(CLK), .D(Q1), .Q(FF1_q));  // open: Qn, preset, en, reset
  and g6 (g6_out, FF1_q, SHIFT_LOAD);
  and g3 (g3_out, not_1_out, D2);
  or or_2 (Q2, g6_out, g3_out);
  D_Flip_Flop FF2 (.clk(CLK), .D(Q2), .Q(FF2_q));  // open: Qn, preset, en, reset
  and g7 (g7_out, FF2_q, SHIFT_LOAD);
  and g4 (g4_out, not_1_out, D3);
  or or_3 (Q3, g7_out, g4_out);
  D_Flip_Flop FF3 (.clk(CLK), .D(Q3));  // open: Q, Qn, preset, en, reset
endmodule
