// Logisim project pchecker.circ as structural Verilog: 1 circuit, main circuit main
module main (
  input  B0,
  input  B1,
  input  B2,
  input  B3,
  input  SHIFT_LOAD,
  output P
);

  wire CLK_out, main_1_q0, main_1_q1, main_1_q2, main_1_q3, xor_1_out, xor_2_out;

  Clock CLK (.out(CLK_out));
  xor xor_1 (xor_1_out, main_1_q0, main_1_q1);
  parity_main main_1 (
    .SHIFT_LOAD(SHIFT_LOAD), .CLK(CLK_out), .D0(B0), .D1(B1), .D2(B2), .D3(B3), .Q0(main_1_q0),
    .Q1(main_1_q1), .Q2(main_1_q2), .Q3(main_1_q3));
  xor xor_2 (xor_2_out, main_1_q2, main_1_q3);
  xor xor_3 (P, xor_1_out, xor_2_out);

  // Notes on the sheet:
  //   código corrigido com a colaboração do professor CESAR GIACOMINI PENTEADO, aquele que cedeu os slides que foram usados como base
  //   versão inicial de "parity" realizado pelo professor CESAR GIACOMINI PENTEADO
  //   código realizado por João Paulo Ferrari Sant'Ana dia 11/11/24 as 22:17
endmodule
