// Logisim project ra.circ as structural Verilog: 1 circuit, main circuit main
module main (
  input  RST_global
);

  wire and_1_out, and_2_out, and_3_out, and_4_out, and_5_out, and_6_out, and_7_out, clock_global_out,
       decodiicador7seg_1_a_2, decodiicador7seg_1_b_2, decodiicador7seg_1_c_2, decodiicador7seg_1_d_2,
       decodiicador7seg_1_e, decodiicador7seg_1_f, decodiicador7seg_1_g, decodiicador7seg_2_a_2,
       decodiicador7seg_2_b_2, decodiicador7seg_2_c_2, decodiicador7seg_2_d_2, decodiicador7seg_2_e,
       decodiicador7seg_2_f, decodiicador7seg_2_g, decodiicador7seg_3_a_2, decodiicador7seg_3_b_2,
       decodiicador7seg_3_c_2, decodiicador7seg_3_d_2, decodiicador7seg_3_e, decodiicador7seg_3_f,
       decodiicador7seg_3_g, decodiicador7seg_4_a_2, decodiicador7seg_4_b_2, decodiicador7seg_4_c_2,
       decodiicador7seg_4_d_2, decodiicador7seg_4_e, decodiicador7seg_4_f, decodiicador7seg_4_g,
       decodiicador7seg_5_a_2, decodiicador7seg_5_b_2, decodiicador7seg_5_c_2, decodiicador7seg_5_d_2,
       decodiicador7seg_5_e, decodiicador7seg_5_f, decodiicador7seg_5_g, decodiicador7seg_6_a_2,
       decodiicador7seg_6_b_2, decodiicador7seg_6_c_2, decodiicador7seg_6_d_2, decodiicador7seg_6_e,
       decodiicador7seg_6_f, decodiicador7seg_6_g, decodiicador7seg_7_a_2, decodiicador7seg_7_b_2,
       decodiicador7seg_7_c_2, decodiicador7seg_7_d_2, decodiicador7seg_7_e, decodiicador7seg_7_f,
       decodiicador7seg_7_g, main_1_q0, main_1_q1, main_1_q2, main_1_q3, main_2_q0, main_2_q1, main_2_q2,
       main_2_q3, main_3_q0, main_3_q1, main_3_q2, main_3_q3, main_4_q0, main_4_q1, main_4_q2, main_4_q3,
       main_5_q0, main_5_q1, main_5_q2, main_5_q3, main_6_q0, main_6_q1, main_6_q2, main_6_q3, main_7_q0,
       main_7_q1, main_7_q2, main_7_q3, or_1_out, or_2_out, or_3_out, or_4_out, or_5_out;

  Clock clock_global (.out(clock_global_out));
  or or_1 (or_1_out, and_1_out, clock_global_out);
  or or_2 (or_2_out, and_4_out, clock_global_out);
  and and_1 (and_1_out, main_1_q1, main_1_q1);
  and and_2 (and_2_out, main_2_q0, main_2_q0);
  and and_3 (and_3_out, main_3_q0, main_3_q0);
  and and_4 (and_4_out, main_4_q2, main_4_q1, main_4_q0);
  and and_5 (and_5_out, main_5_q3, main_5_q3);
  or or_3 (or_3_out, and_5_out, clock_global_out);
  or or_4 (or_4_out, and_6_out, clock_global_out);
  or or_5 (or_5_out, and_7_out, clock_global_out);
  and and_6 (and_6_out, main_6_q2, main_6_q0);
  and and_7 (and_7_out, main_7_q2, main_7_q1, main_7_q0);
  DECODIICADOR7SEG decodiicador7seg_1 (
    .A(main_1_q3), .B(main_1_q2), .C(main_1_q1), .D(main_1_q0), .a_2(decodiicador7seg_1_a_2),
    .b_2(decodiicador7seg_1_b_2), .c_2(decodiicador7seg_1_c_2), .d_2(decodiicador7seg_1_d_2),
    .e(decodiicador7seg_1_e), .f(decodiicador7seg_1_f), .g(decodiicador7seg_1_g));
  counter_main main_1 (
    .CLK(or_1_out), .RST(RST_global), .Q0(main_1_q0), .Q1(main_1_q1), .Q2(main_1_q2), .Q3(main_1_q3));
  counter_main main_2 (
    .CLK(clock_global_out), .RST(and_2_out), .Q0(main_2_q0), .Q1(main_2_q1), .Q2(main_2_q2), .Q3(main_2_q3));
  counter_main main_3 (
    .CLK(clock_global_out), .RST(and_3_out), .Q0(main_3_q0), .Q1(main_3_q1), .Q2(main_3_q2), .Q3(main_3_q3));
  counter_main main_4 (
    .CLK(or_2_out), .RST(RST_global), .Q0(main_4_q0), .Q1(main_4_q1), .Q2(main_4_q2), .Q3(main_4_q3));
  counter_main main_5 (
    .CLK(or_3_out), .RST(RST_global), .Q0(main_5_q0), .Q1(main_5_q1), .Q2(main_5_q2), .Q3(main_5_q3));
  counter_main main_6 (
    .CLK(or_4_out), .RST(RST_global), .Q0(main_6_q0), .Q1(main_6_q1), .Q2(main_6_q2), .Q3(main_6_q3));
  counter_main main_7 (
    .CLK(or_5_out), .RST(RST_global), .Q0(main_7_q0), .Q1(main_7_q1), .Q2(main_7_q2), .Q3(main_7_q3));
  _7_Segment_Display u_7_segment_display_1 (
    .g(decodiicador7seg_1_g), .f(decodiicador7seg_1_f), .a(decodiicador7seg_1_a_2),
    .b(decodiicador7seg_1_b_2), .e(decodiicador7seg_1_e), .d(decodiicador7seg_1_d_2),
    .c(decodiicador7seg_1_c_2));  // open: dp
  DECODIICADOR7SEG decodiicador7seg_2 (
    .A(main_2_q3), .B(main_2_q2), .C(main_2_q1), .D(main_2_q0), .a_2(decodiicador7seg_2_a_2),
    .b_2(decodiicador7seg_2_b_2), .c_2(decodiicador7seg_2_c_2), .d_2(decodiicador7seg_2_d_2),
    .e(decodiicador7seg_2_e), .f(decodiicador7seg_2_f), .g(decodiicador7seg_2_g));
  DECODIICADOR7SEG decodiicador7seg_3 (
    .A(main_3_q3), .B(main_3_q2), .C(main_3_q1), .D(main_3_q0), .a_2(decodiicador7seg_3_a_2),
    .b_2(decodiicador7seg_3_b_2), .c_2(decodiicador7seg_3_c_2), .d_2(decodiicador7seg_3_d_2),
    .e(decodiicador7seg_3_e), .f(decodiicador7seg_3_f), .g(decodiicador7seg_3_g));
  DECODIICADOR7SEG decodiicador7seg_4 (
    .A(main_4_q3), .B(main_4_q2), .C(main_4_q1), .D(main_4_q0), .a_2(decodiicador7seg_4_a_2),
    .b_2(decodiicador7seg_4_b_2), .c_2(decodiicador7seg_4_c_2), .d_2(decodiicador7seg_4_d_2),
    .e(decodiicador7seg_4_e), .f(decodiicador7seg_4_f), .g(decodiicador7seg_4_g));
  DECODIICADOR7SEG decodiicador7seg_5 (
    .A(main_5_q3), .B(main_5_q2), .C(main_5_q1), .D(main_5_q0), .a_2(decodiicador7seg_5_a_2),
    .b_2(decodiicador7seg_5_b_2), .c_2(decodiicador7seg_5_c_2), .d_2(decodiicador7seg_5_d_2),
    .e(decodiicador7seg_5_e), .f(decodiicador7seg_5_f), .g(decodiicador7seg_5_g));
  DECODIICADOR7SEG decodiicador7seg_6 (
    .A(main_6_q3), .B(main_6_q2), .C(main_6_q1), .D(main_6_q0), .a_2(decodiicador7seg_6_a_2),
    .b_2(decodiicador7seg_6_b_2), .c_2(decodiicador7seg_6_c_2), .d_2(decodiicador7seg_6_d_2),
    .e(decodiicador7seg_6_e), .f(decodiicador7seg_6_f), .g(decodiicador7seg_6_g));
  DECODIICADOR7SEG decodiicador7seg_7 (
    .A(main_7_q3), .B(main_7_q2), .C(main_7_q1), .D(main_7_q0), .a_2(decodiicador7seg_7_a_2),
    .b_2(decodiicador7seg_7_b_2), .c_2(decodiicador7seg_7_c_2), .d_2(decodiicador7seg_7_d_2),
    .e(decodiicador7seg_7_e), .f(decodiicador7seg_7_f), .g(decodiicador7seg_7_g));
  _7_Segment_Display u_7_segment_display_2 (
    .g(decodiicador7seg_2_g), .f(decodiicador7seg_2_f), .a(decodiicador7seg_2_a_2),
    .b(decodiicador7seg_2_b_2), .e(decodiicador7seg_2_e), .d(decodiicador7seg_2_d_2),
    .c(decodiicador7seg_2_c_2));  // open: dp
  _7_Segment_Display u_7_segment_display_3 (
    .g(decodiicador7seg_4_g), .f(decodiicador7seg_4_f), .a(decodiicador7seg_4_a_2),
    .b(decodiicador7seg_4_b_2), .e(decodiicador7seg_4_e), .d(decodiicador7seg_4_d_2),
    .c(decodiicador7seg_4_c_2));  // open: dp
  _7_Segment_Display u_7_segment_display_4 (
    .g(decodiicador7seg_3_g), .f(decodiicador7seg_3_f), .a(decodiicador7seg_3_a_2),
    .b(decodiicador7seg_3_b_2), .e(decodiicador7seg_3_e), .d(decodiicador7seg_3_d_2),
    .c(decodiicador7seg_3_c_2));  // open: dp
  _7_Segment_Display u_7_segment_display_5 (
    .g(decodiicador7seg_5_g), .f(decodiicador7seg_5_f), .a(decodiicador7seg_5_a_2),
    .b(decodiicador7seg_5_b_2), .e(decodiicador7seg_5_e), .d(decodiicador7seg_5_d_2),
    .c(decodiicador7seg_5_c_2));  // open: dp
  _7_Segment_Display u_7_segment_display_6 (
    .g(decodiicador7seg_6_g), .f(decodiicador7seg_6_f), .a(decodiicador7seg_6_a_2),
    .b(decodiicador7seg_6_b_2), .e(decodiicador7seg_6_e), .d(decodiicador7seg_6_d_2),
    .c(decodiicador7seg_6_c_2));  // open: dp
  _7_Segment_Display u_7_segment_display_7 (
    .g(decodiicador7seg_7_g), .f(decodiicador7seg_7_f), .a(decodiicador7seg_7_a_2),
    .b(decodiicador7seg_7_b_2), .e(decodiicador7seg_7_e), .d(decodiicador7seg_7_d_2),
    .c(decodiicador7seg_7_c_2));  // open: dp

  // Notes on the sheet:
  //   pare de aumentar quando chegar no dois
  //   não aumente
  //   não aumente
  //   pare de aumentar quando chegar no sete
  //   pare de aumentar quando chegar no oitio
  //   pare de aumentar quando chegar no cinco
  //   pare de aumentar quando chegar no sete
  //   código realizado por João Paulo Ferrari Sant' Ana
  //   terminado dia 9/11/24 as 15:07
endmodule
