// Logisim project contadordesc.circ as structural Verilog: 1 circuit, main circuit main
module main (
  input  CLK,
  input  RST,
  input  PST,
  output Q0,
  output Q1,
  output Q2,
  output Q3
);

  wire and_1_out, and_2_out, j_k_ff_1_qn, j_k_ff_2_qn, j_k_ff_3_qn;

  J_K_Flip_Flop j_k_ff_1 (
    .J(1'b1), .clk(CLK), .K(1'b1), .Q(Q0), .Qn(j_k_ff_1_qn), .preset(PST), .reset(RST));  // open: en
  J_K_Flip_Flop j_k_ff_2 (
    .J(j_k_ff_1_qn), .clk(CLK), .K(j_k_ff_1_qn), .Q(Q1), .Qn(j_k_ff_2_qn), .preset(PST), .reset(RST));  // open: en
  and and_1 (and_1_out, j_k_ff_1_qn, j_k_ff_2_qn);
  and and_2 (and_2_out, and_1_out, j_k_ff_3_qn);
  J_K_Flip_Flop j_k_ff_3 (
    .J(and_1_out), .clk(CLK), .K(and_1_out), .Q(Q2), .Qn(j_k_ff_3_qn), .preset(PST), .reset(RST));  // open: en
  J_K_Flip_Flop j_k_ff_4 (.J(and_2_out), .clk(CLK), .K(and_2_out), .Q(Q3), .preset(PST), .reset(RST));  // open: Qn, en

  // Notes on the sheet:
  //   https://www.electronics-tutorials.ws/counter/count_4.html
endmodule
