// Logisim project decrecentcounter.circ as structural Verilog: 1 circuit, main circuit main
module main (
  input  CLK,
  input  S0,
  input  S1,
  input  S3,
  input  S4,
  input  RST,
  output Q0,
  output Q1,
  output Q2,
  output Q3
);

  wire and_1_out, and_2_out, j_k_ff_1_qn, j_k_ff_2_qn, j_k_ff_3_qn, j_k_ff_4_qn;

  J_K_Flip_Flop j_k_ff_1 (
    .J(1'b1), .clk(CLK), .K(1'b1), .Q(Q0), .Qn(j_k_ff_1_qn), .preset(S0), .reset(RST));  // open: en
  J_K_Flip_Flop j_k_ff_2 (
    .J(j_k_ff_1_qn), .clk(CLK), .K(j_k_ff_1_qn), .Q(Q1), .Qn(j_k_ff_2_qn), .preset(S1), .reset(RST));  // open: en
  and and_1 (and_1_out, j_k_ff_1_qn, j_k_ff_2_qn);
  and and_2 (and_2_out, and_1_out, j_k_ff_3_qn);
  J_K_Flip_Flop j_k_ff_3 (
    .J(and_1_out), .clk(CLK), .K(and_1_out), .Q(Q2), .Qn(j_k_ff_3_qn), .preset(S3), .reset(RST));  // open: en
  J_K_Flip_Flop j_k_ff_4 (
    .J(and_2_out), .clk(CLK), .K(and_2_out), .Q(Q3), .Qn(j_k_ff_4_qn), .preset(S4), .reset(RST));  // open: en

  // Notes on the sheet:
  //   versão inicial baseada em: https://www.electronics-tutorials.ws/counter/count_4.html
  //   dica obtida pelo Cesar Giacomini Penteado
endmodule
