// Logisim project regress.circ as structural Verilog: 1 circuit, main circuit main
module main (
  input  RST,
  input  in_2,
  input  in_3,
  input  in_4,
  input  in_5,
  input  RST_2,
  input  in_7,
  input  in_8,
  input  in_9,
  input  in_10
);

  wire and_1_out, and_2_out, CLK_2_out, CLK_out, decodiicador7seg_1_a_2, decodiicador7seg_1_b_2,
       decodiicador7seg_1_c_2, decodiicador7seg_1_d_2, decodiicador7seg_1_e, decodiicador7seg_1_f,
       decodiicador7seg_1_g, decodiicador7seg_2_a_2, decodiicador7seg_2_b_2, decodiicador7seg_2_c_2,
       decodiicador7seg_2_d_2, decodiicador7seg_2_e, decodiicador7seg_2_f, decodiicador7seg_2_g, main_1_q0,
       main_1_q1, main_1_q2, main_1_q3, main_2_q0, main_2_q1, main_2_q2, main_2_q3, not_1_out, not_2_out,
       not_3_out, not_4_out, not_5_out, not_6_out, not_7_out, not_8_out, or_1_out, undriven;

  Clock CLK (.out(CLK_out));
  or or_1 (or_1_out, CLK_out, and_1_out);
  decrecentcounter_main main_1 (
    .CLK(or_1_out), .RST(RST), .S0(in_2), .Q0(main_1_q0), .S1(in_3), .Q1(main_1_q1), .S3(in_4),
    .Q2(main_1_q2), .S4(in_5), .Q3(main_1_q3));
  Clock CLK_2 (.out(CLK_2_out));
  not not_1 (not_1_out, main_1_q0);
  decrecentcounter_main main_2 (
    .CLK(undriven), .RST(RST_2), .S0(in_7), .Q0(main_2_q0), .S1(in_8), .Q1(main_2_q1), .S3(in_9),
    .Q2(main_2_q2), .S4(in_10), .Q3(main_2_q3));
  not not_2 (not_2_out, main_1_q3);
  not not_3 (not_3_out, main_1_q2);
  not not_4 (not_4_out, main_1_q1);
  and and_1 (and_1_out, not_1_out, not_4_out, not_3_out, not_2_out);
  LED led_1 (.in(and_1_out));
  not not_5 (not_5_out, main_2_q2);
  not not_6 (not_6_out, main_2_q1);
  not not_7 (not_7_out, main_2_q0);
  and and_2 (and_2_out, not_7_out, not_6_out, not_5_out, not_8_out);
  DECODIICADOR7SEG decodiicador7seg_1 (
    .A(main_1_q3), .B(main_1_q2), .C(main_1_q1), .D(main_1_q0), .a_2(decodiicador7seg_1_a_2),
    .b_2(decodiicador7seg_1_b_2), .c_2(decodiicador7seg_1_c_2), .d_2(decodiicador7seg_1_d_2),
    .e(decodiicador7seg_1_e), .f(decodiicador7seg_1_f), .g(decodiicador7seg_1_g));
  not not_8 (not_8_out, main_2_q3);
  LED led_2 (.in(and_2_out));
  _7_Segment_Display u_7_segment_display_1 (
    .g(decodiicador7seg_1_g), .f(decodiicador7seg_1_f), .a(decodiicador7seg_1_a_2),
    .b(decodiicador7seg_1_b_2), .e(decodiicador7seg_1_e), .d(decodiicador7seg_1_d_2),
    .c(decodiicador7seg_1_c_2));  // open: dp
  DECODIICADOR7SEG decodiicador7seg_2 (
    .A(main_2_q3), .B(main_2_q2), .C(main_2_q1), .D(main_2_q0), .a_2(decodiicador7seg_2_a_2),
    .b_2(decodiicador7seg_2_b_2), .c_2(decodiicador7seg_2_c_2), .d_2(decodiicador7seg_2_d_2),
    .e(decodiicador7seg_2_e), .f(decodiicador7seg_2_f), .g(decodiicador7seg_2_g));
  _7_Segment_Display u_7_segment_display_2 (
    .g(decodiicador7seg_2_g), .f(decodiicador7seg_2_f), .a(decodiicador7seg_2_a_2),
    .b(decodiicador7seg_2_b_2), .e(decodiicador7seg_2_e), .d(decodiicador7seg_2_d_2),
    .c(decodiicador7seg_2_c_2));  // open: dp

  // Notes on the sheet:
  //   Sinal de fim da contagem
  //   Sinal de fim da contagem
  //   código realizado por João Paulo  Ferrari Sant'Ana, dia 15/11/24 ás 17:02
  //   dica de como desenvolver circuto obtido a partir do professor CESAR GIACOMINI PENTEADO
  //   dia 11/11/24 as 10:20PM
endmodule
