// Logisim project serial-entry-paralel-exit.circ as structural Verilog: 1 circuit, main circuit main
module main (
  input  CLK,
  input  data_in,
  output out_3,
  output out_4,
  output out_5
);

  D_Flip_Flop d_ff_1 (.clk(CLK), .D(data_in), .Q(out_3));  // open: Qn, preset, en, reset
  D_Flip_Flop d_ff_2 (.clk(CLK), .D(out_3), .Q(out_4));  // open: Qn, preset, en, reset
  D_Flip_Flop d_ff_3 (.clk(CLK), .D(out_4), .Q(out_5));  // open: Qn, preset, en, reset
  D_Flip_Flop d_ff_4 (.clk(CLK), .D(out_5));  // open: Q, Qn, preset, en, reset
endmodule
