// Logisim project subtr2.circ as structural Verilog: 1 circuit, main circuit main
module main (
  input  C1,
  input  B0,
  input  A0,
  input  B1,
  input  A1,
  input  B2,
  input  A2,
  input  B3,
  input  A3,
  output out_10,
  output D0,
  output out_12,
  output out_13,
  output out_14,
  output D1,
  output out_16,
  output C1_2,
  output out_18,
  output D2,
  output out_20,
  output C2,
  output out_22,
  output D3,
  output out_24,
  output C3
);

  wire and_5_out, and_6_out, and_7_out, and_8_out, not_1_out, not_2_out, not_3_out, not_4_out, not_5_out,
       not_6_out, not_7_out, not_8_out;

  xor xor_1 (out_10, B0, A0);
  not not_1 (not_1_out, B0);
  xor xor_2 (out_14, B1, A1);
  not not_2 (not_2_out, B1);
  xor xor_3 (out_18, B2, A2);
  not not_3 (not_3_out, B2);
  xor xor_4 (out_22, B3, A3);
  not not_4 (not_4_out, B3);
  LED led_1 (.in(out_10));
  and and_1 (out_12, not_1_out, A0);
  LED led_2 (.in(out_14));
  and and_2 (out_16, not_2_out, A1);
  LED led_3 (.in(out_18));
  and and_3 (out_20, not_3_out, A2);
  LED led_4 (.in(out_22));
  and and_4 (out_24, not_4_out, A3);
  LED led_5 (.in(out_12));
  LED led_6 (.in(out_16));
  LED led_7 (.in(out_20));
  LED led_8 (.in(out_24));
  not not_5 (not_5_out, out_10);
  not not_6 (not_6_out, out_14);
  not not_7 (not_7_out, out_18);
  not not_8 (not_8_out, out_22);
  xor xor_5 (D0, C1, out_10);
  and and_5 (and_5_out, not_5_out, C1);
  xor xor_6 (D1, out_13, out_14);
  xor xor_7 (D2, C1_2, out_18);
  LED led_9 (.in(D3));
  xor xor_8 (D3, C2, out_22);
  and and_6 (and_6_out, not_8_out, C2);
  LED led_10 (.in(D0));
  LED led_11 (.in(D1));
  and and_7 (and_7_out, not_6_out, out_13);
  LED led_12 (.in(D2));
  and and_8 (and_8_out, not_7_out, C1_2);
  or or_1 (out_13, and_5_out, out_12);
  or or_2 (C1_2, and_7_out, out_16);
  or or_3 (C2, and_8_out, out_20);
  or or_4 (C3, and_6_out, out_24);
endmodule
